# Fritzing sketch LoRa_shield (saved by Fritzing 0.9.3b)
perfboards: 1

parts:
  M1 = Osoyoo SX1278-ra-02
  LLC1 = Logic Level Converter [package="Breakout board"]
  U3 = Voltage Regulator -- 3.3 V -- AMS1117
  Arduino_Digital_PWM_Intrupt = male pin header, 18 pins [form="♂ (male)"]
  Arduino_AnalogPins = male pin header, 6 pins [form="♂ (male)"]  # not connected
  IR_2 = female pin header, 3 pins [form="♀ (female)"]
  IR_1 = female pin header, 3 pins [form="♀ (female)"]
  IR_3 = female pin header, 3 pins [form="♀ (female)"]
  Arduino_powerPins = Generic double row male header - 8 pins [form="♂ (male)" package=THT]
  J1 = female pin header, 4 pins [form="♀ (female)"]

nets:
  N1: M1.GND, IR_2.pin2, IR_1.pin2, IR_3.pin2, Arduino_powerPins.pin7
  N2: M1.3.3V, LLC1.LV, U3.OUT
  N3: M1.DIO0, Arduino_Digital_PWM_Intrupt.pin16
  N4: M1.SCK, LLC1.LV1
  N5: M1.MISO, LLC1.LV2
  N6: M1.MOSI, LLC1.LV3
  N7: M1.NSS, LLC1.LV4
  N8: LLC1.HV4, Arduino_Digital_PWM_Intrupt.pin8
  N9: LLC1.HV3, Arduino_Digital_PWM_Intrupt.pin7
  N10: LLC1.HV, IR_2.pin1, IR_1.pin1, IR_3.pin1, Arduino_powerPins.pin2, J1.pin2
  N11: LLC1.HV2, Arduino_Digital_PWM_Intrupt.pin6
  N12: LLC1.HV1, Arduino_Digital_PWM_Intrupt.pin5
  N13: U3.GND, Arduino_powerPins.pin6, J1.pin1
  N14: U3.IN, Arduino_powerPins.pin5
  N15: Arduino_Digital_PWM_Intrupt.pin1, J1.pin4
  N16: Arduino_Digital_PWM_Intrupt.pin2, J1.pin3
  N17: Arduino_Digital_PWM_Intrupt.pin12, IR_3.pin3
  N18: Arduino_Digital_PWM_Intrupt.pin13, IR_2.pin3
  N19: Arduino_Digital_PWM_Intrupt.pin14, IR_1.pin3

notes:
  pin6
  pin5
  pin4
  pin2
  SDA
  SCL

custom parts:
  Osoyoo SX1278-ra-02: Osoyoo Long Distance wireless transceiver Uart LoRa Module.
  Logic Level Converter: 5V to/from 3.3V logic level converter
  Voltage Regulator -- 3.3 V -- AMS1117: AMS1117 3.3v module
  Generic double row male header - 8 pins: Generic double row male header
