# Fritzing sketch Lora (saved by Fritzing 0.9.3b)
perfboards: 1

parts:
  J1 = female pin header, 8 pins [form="♀ (female)"]
  J2 = female pin header, 6 pins [form="♀ (female)"]
  J3 = female pin header, 18 pins [form="♀ (female)"]
  M1 = Osoyoo SX1278-ra-02
  LLC1 = Logic Level Converter [package="Breakout board"]
  PH-4502c = Generic female header - 6 pins [form="♀ (female)" package=THT]
  AJ-SR04m = Generic female header - 4 pins [form="♀ (female)" package=THT]
  DS18B20 = Generic female header - 3 pins [form="♀ (female)" package=THT]
  AMS1117_3_3V1 = Voltage Regulator -- 3.3 V -- AMS1117

nets:
  5V: J1.pin2, LLC1.HV, AJ-SR04m.5V, DS18B20.Vcc
  N1: J1.pin5, AMS1117_3_3V1.IN
  N2: J1.pin7, AMS1117_3_3V1.GND
  N3: J2.pin6, PH-4502c.Po
  N4: J3.pin5, LLC1.HV2
  N5: J3.pin6, LLC1.HV1
  N6: J3.pin7, LLC1.HV3
  N7: J3.pin8, LLC1.HV4
  N8: J3.pin10, DS18B20.Dq
  N9: J3.pin12, AJ-SR04m.TRIG
  N10: J3.pin13, AJ-SR04m.ECHO
  GND: M1.GND, LLC1.L-GND, PH-4502c.GND, AJ-SR04m.GND
  N11: M1.3.3V, LLC1.LV, AMS1117_3_3V1.OUT
  N12: M1.SCK, LLC1.LV2
  N13: M1.MISO, LLC1.LV1
  N14: M1.MOSI, LLC1.LV3
  N15: M1.NSS, LLC1.LV4
  N16: LLC1.H-GND, DS18B20.GND

notes:
  5V
  RES
  3.3V
  GND
  VIN
  A0
  A6
  SCL
  SDA
  AREF
  13
  8
  7
  0

custom parts:
  Osoyoo SX1278-ra-02: Osoyoo Long Distance wireless transceiver Uart LoRa Module.
  Logic Level Converter: 5V to/from 3.3V logic level converter
  Generic female header - 6 pins: Generic female header
  Generic female header - 4 pins: Generic female header
  Generic female header - 3 pins: Generic female header
  Voltage Regulator -- 3.3 V -- AMS1117: AMS1117 3.3v module
