# Fritzing sketch debounce_circuit (saved by Fritzing 0.9.3b)
perfboards: 1

parts:
  R1 = Resistor [tolerance=±5% resistance=220 package=THT]
  R2 = Resistor [tolerance=±5% resistance=220 package=THT]
  D1 = Rectifier Diode [part_number=1N4001 package="300 mil [THT]"]
  C1 = Electrolytic Capacitor [capacitance=1µF package="100 mil [THT, electrolytic]"]
  IC1 = IC, DIP package, 14 pins [chip_label=IC]
  S1 = Round Pushbutton
  R3 = Resistor [tolerance=±5% resistance=220 package=THT]
  R4 = Resistor [tolerance=±5% resistance=220 package=THT]
  D2 = Rectifier Diode [part_number=1N4001 package="300 mil [THT]"]
  C2 = Electrolytic Capacitor [capacitance=1µF package="100 mil [THT, electrolytic]"]
  S2 = Round Pushbutton
  R5 = Resistor [tolerance=±5% resistance=220 package=THT]
  R6 = Resistor [tolerance=±5% resistance=220 package=THT]
  D3 = Rectifier Diode [part_number=1N4001 package="300 mil [THT]"]
  C3 = Electrolytic Capacitor [capacitance=1µF package="100 mil [THT, electrolytic]"]
  S3 = Round Pushbutton
  J1 = male pin header, 3 pins [form="♂ (male)"]
  J2 = female pin header, 2 pins [form="♀ (female)"]

nets:
  N1: R1.Pin_0, R2.Pin_0, D1.anode, S1.leg1
  5V: R1.Pin_1, IC1.pin14, R4.Pin_1, R6.Pin_1, J2.pin1
  N2: R2.Pin_1, D1.cathode, C1.+, IC1.pin5
  GND: C1.-, IC1.pin7, S1.leg0, C2.-, S2.leg0, C3.-, S3.leg0, J2.pin2
  N3: IC1.pin1, R5.Pin_1, D3.cathode, C3.+
  N4: IC1.pin2, J1.pin1
  N5: IC1.pin3, R3.Pin_1, D2.cathode, C2.+
  N6: IC1.pin4, J1.pin2
  N7: IC1.pin6, J1.pin3
  N8: R3.Pin_0, R4.Pin_0, D2.anode, S2.leg1
  N9: R5.Pin_0, R6.Pin_0, D3.anode, S3.leg1
