# Fritzing sketch esp8266_LoRa_schematic (saved by Fritzing 0.9.3b)
perfboards: 1

parts:
  U1 = ESP8266 NodeMCU LoLin module
  M1 = Osoyoo SX1278-ra-02

nets:
  N1: U1.D2, M1.DIO0
  3V3: U1.3V3, M1.3.3V
  N2: U1.D5, M1.SCK
  N3: U1.D6, M1.MISO
  N4: U1.D7, M1.MOSI
  N5: U1.D8, M1.NSS
  GND: U1.GND, M1.GND

custom parts:
  ESP8266 NodeMCU LoLin module: ESP8266 based NodeMCU
  Osoyoo SX1278-ra-02: Osoyoo Long Distance wireless transceiver Uart LoRa Module.
