# Fritzing sketch fishcounter_schematic (saved by Fritzing 0.9.3b)
perfboards: 1

parts:
  Part1 = Arduino Uno (Rev3)
  M1 = Osoyoo SX1278-ra-02
  LLC1 = Logic Level Converter [package="Breakout board"]
  IR_1 = fc-51 [package=THT]
  IR_2 = fc-51 [package=THT]
  IR_3 = fc-51 [package=THT]
  LCM1602_IIC1 = LCM1602 IIC [part_number="LCM1602 IIC" chip_label="LCM1602 IIC" package="DIP (Dual Inline) [THT]"]
  interrupt_btn = Round Pushbutton
  longpress_btn = Round Pushbutton

nets:
  N1: Part1.A4/SDA, LCM1602_IIC1.SDA
  N2: Part1.A5/SCL, LCM1602_IIC1.SCL
  N3: Part1.D10_PWM/SS, LLC1.HV4
  N4: Part1.D11_PWM/MOSI, LLC1.HV3
  N5: Part1.D12/MISO, LLC1.HV2
  N6: Part1.D13/SCK, LLC1.HV1
  GND: Part1.GND, M1.GND, IR_1.pin2, IR_2.pin2, IR_3.pin2, LCM1602_IIC1.GND, interrupt_btn.leg1, longpress_btn.leg1
  N7: Part1.D2, M1.DIO0
  N8: Part1.D3_PWM, interrupt_btn.leg0
  N9: Part1.D4, IR_1.pin1
  N10: Part1.D5_PWM, IR_2.pin1
  N11: Part1.D6_PWM, IR_3.pin1
  N12: Part1.D7, longpress_btn.leg0
  3V3: Part1.3V3, M1.3.3V, LLC1.LV
  5V: Part1.5V, LLC1.HV, IR_1.pin3, IR_2.pin3, IR_3.pin3, LCM1602_IIC1.VCC
  N13: M1.SCK, LLC1.LV1
  N14: M1.MISO, LLC1.LV2
  N15: M1.MOSI, LLC1.LV3
  N16: M1.NSS, LLC1.LV4

custom parts:
  Osoyoo SX1278-ra-02: Osoyoo Long Distance wireless transceiver Uart LoRa Module.
  Logic Level Converter: 5V to/from 3.3V logic level converter
  LCM1602 IIC: I2C-Module to use a 1602 or 2004 LCD on with the wire.h libory Serial LCD Modul
