# Fritzing sketch power circuit02 (saved by Fritzing 0.9.3b)
perfboards: 1

parts:
  U1 = 555 Timer [package="DIP8 [THT]"]
  C1 = Electrolytic Capacitor [capacitance=0.1mF package="100 mil [THT, electrolytic]"]
  Q1 = NPN-Transistor [package="TO92 [THT]"]
  Q2 = PNP-Transistor [package="TO92 [THT]"]
  S1 = Pushbutton [package=THT]
  R2 = Resistor [tolerance=±5% resistance=1k package=THT]
  R4 = Resistor [tolerance=±5% resistance=220k package=THT]
  C2 = Electrolytic Capacitor [capacitance=10µF package="100 mil [THT, electrolytic]"]
  R5 = Resistor [tolerance=±5% resistance=220 package=THT]
  J2 = Screw terminal - 2 pins [package=THT]
  R7 = Resistor [tolerance=±5% resistance=1k package=THT]
  IC1 = IC, DIP package, 16 pins [chip_label=CD4017]
  J3 = Screw terminal - 2 pins [package=THT]
  Q3 = NPN-Transistor [package="TO92 [THT]"]
  J4 = Screw terminal - 2 pins [package=THT]
  J5 = Screw terminal - 2 pins [package=THT]
  VCC1 = Battery block 9V
  VCC2 = Battery block 9V
  R3 = Resistor [tolerance=±5% resistance=1k package=THT]
  R6 = Resistor [tolerance=±5% resistance=1k package=THT]
  R1 = Resistor [tolerance=±5% resistance=4.7k package=THT]

nets:
  N1: U1.Ground, C1.-, Q1.E, C2.-, IC1.pin8, IC1.pin13, J3.pin2, Q3.E, J5.pin2, VCC1.-, VCC2.-, R1.Pin_1
  N2: U1.Trigger, U1.Threshold, R4.Pin_1, C2.+
  N3: U1.Output, R6.Pin_1
  N4: U1.Vcc_Supply_Voltage, Q2.E, S1.leg1, R4.Pin_0
  N5: C1.+, R2.Pin_0, IC1.pin14, R1.Pin_0
  N6: Q1.B, R5.Pin_1, Q3.B
  N7: Q1.C, J2.pin1
  N8: Q2.B, R3.Pin_0
  N9: Q2.C, R7.Pin_1
  N10: S1.leg0, J2.pin2, IC1.pin16, J3.pin1, VCC2.+
  N11: R2.Pin_1, R7.Pin_0
  N12: R5.Pin_0, IC1.pin2
  N13: IC1.pin4, IC1.pin15
  N14: Q3.C, J4.pin1
  N15: J4.pin2, J5.pin1, VCC1.+
  N16: R3.Pin_1, R6.Pin_0

notes:
  1k
  4.7
  220k
  220
