# Fritzing sketch watermonitor_solder (saved by Fritzing 0.9.3b)
perfboards: 1

parts:
  Part1 = Arduino Uno (Rev3)
  LCM1602_IIC1 = LCM1602 IIC [part_number="LCM1602 IIC" chip_label="LCM1602 IIC" package="DIP (Dual Inline) [THT]"]
  ph_sensor = ph-4502c [package=THT]
  DS1 = DS18B20 1-Wire Temperature Sensor [part_number=DS18B20]
  M1 = Osoyoo SX1278-ra-02
  LLC1 = Logic Level Converter [package="Breakout board"]
  interrupt_pin = Square Pushbutton
  longpress_btn = Square Pushbutton
  Amp-Volt_converter = Generic female header - 3 pins [form="♀ (female)" package=THT]

nets:
  N1: Part1.A0, ph_sensor.pin3
  N2: Part1.A2, Amp-Volt_converter.DQ
  N3: Part1.A4/SDA, LCM1602_IIC1.SDA
  N4: Part1.A5/SCL, LCM1602_IIC1.SCL
  N5: Part1.D8, DS1.DQ
  N6: Part1.D10_PWM/SS, LLC1.HV4
  N7: Part1.D11_PWM/MOSI, LLC1.HV3
  N8: Part1.D12/MISO, LLC1.HV2
  N9: Part1.D13/SCK, LLC1.HV1
  GND: Part1.GND, LCM1602_IIC1.A, LCM1602_IIC1.GND, ph_sensor.pin4, ph_sensor.pin5, DS1.GND, M1.GND, interrupt_pin.leg0, longpress_btn.leg0, Amp-Volt_converter.GND
  N10: Part1.D2, M1.DIO0
  N11: Part1.D3_PWM, interrupt_pin.leg1
  N12: Part1.D7, longpress_btn.leg1
  3V3: Part1.3V3, M1.3.3V, LLC1.LV
  VCC: Part1.5V, LCM1602_IIC1.VCC, ph_sensor.pin6, DS1.VDD, LLC1.HV, Amp-Volt_converter.VCC
  N13: LCM1602_IIC1.RW, M1.DIO3
  N14: M1.SCK, LLC1.LV1
  N15: M1.MISO, LLC1.LV2
  N16: M1.MOSI, LLC1.LV3
  N17: M1.NSS, LLC1.LV4

custom parts:
  LCM1602 IIC: I2C-Module to use a 1602 or 2004 LCD on with the wire.h libory Serial LCD Modul
  ph-4502c: ph-4502c PH Meter.
  Osoyoo SX1278-ra-02: Osoyoo Long Distance wireless transceiver Uart LoRa Module.
  Logic Level Converter: 5V to/from 3.3V logic level converter
  Generic female header - 3 pins: Generic female header
